// Logisim project cpu.circ as structural Verilog: 2 circuits, main circuit main
module main (
  input  [7:0] in_1,
  input  [7:0] in_2
);

  wire a_rd, a_wr, addr, and_7_out, and_8_out, and_9_out, and_10_out, and_11_out, and_12_out, and_13_out,
       and_14_out, and_16_out, and_18_out, and_19_out, and_20_out, and_22_out, and_23_out, and_24_out,
       and_26_out, and_27_out, and_28_out, and_29_out, and_38_out, and_39_out, b_rd, b_wr, bit3, blah,
       branch, c_rd, c_wr, clk, cmp, controlled_buffer_11_out, controlled_buffer_12_out,
       controlled_buffer_13_out, controlled_buffer_14_out, controlled_buffer_15_out,
       controlled_buffer_16_out, d_ff_1_q, d_ff_2_q, decoder_3_out0, decoder_3_out1, decoder_3_out2,
       decoder_3_out3, decoder_3_out4, decoder_3_out5, decoder_3_out6, decoder_3_out7, done, dst_0, dst_1,
       dst_2, dst_3, dst_4, dst_5, dst_6, dst_7, goto, imm, imm2b, invertB, jump, mem, mem_rd, mem_wr, movi,
       nop, nor_1_out, nor_2_out, nor_3_out, nor_4_out, nor_5_out, not_1_out, not_2_out, or_6_out, or_7_out,
       or_14_out, or_15_out, or_16_out, or_17_out, or_18_out, or_19_out, or_20_out, or_21_out, pc_wr, ram_rd,
       ram_wr, src_0, src_1, src_2, src_3, src_4, src_5, src_6, src_7, src_45, src_67, type0, type1, type2,
       wr_en, x_rd, x_wr, y_rd, y_wr;
  wire [2:0] dst, src;
  wire [3:0] alu_1_flags, flags, opcode;
  wire [4:4] register_1_q;
  wire [5:0] controlled_buffer_10_out;
  wire [7:0] A_q, alu_1_alu_out, b, B_q, C_q, controlled_buffer_1_out, controlled_buffer_8_out,
       controlled_inverter_1_out, counter_1_q, MAR_q, multiplexer_1_out, not_3_out, or_10_out, or_12_out,
       pull_resistor_3_node, pull_resistor_6_node, ram_1_dout, rom_1_data, X_q, Y_q;

  RAM #(.enables("line"), .\type ("nonvolatile")) ram_1 (
    .addr(MAR_q), .we(ram_wr), .clk(clk), .din(alu_1_alu_out), .dout(ram_1_dout));
  ROM rom_1 (.addr(counter_1_q), .data(rom_1_data));
  Counter counter_1 (.load(pc_wr), .D(b), .Q(counter_1_q), .clk(clk));  // open: count, carry, up, clr
  Clock clock_1 (.out(clk));
  Decoder #(.select(3)) decoder_1 (
    .out0(src_0), .out1(src_1), .out2(src_2), .out3(src_3), .out4(src_4), .out5(src_5), .out6(src_6),
    .out7(src_7), .sel(src));  // open: en
  Decoder #(.select(3)) decoder_2 (
    .out0(dst_0), .out1(dst_1), .out2(dst_2), .out3(dst_3), .out4(dst_4), .out5(dst_5), .out6(dst_6),
    .out7(dst_7), .sel(dst), .en(type2));
  Register Y (.D(alu_1_alu_out), .en(y_wr), .clk(clk), .Q(Y_q));  // open: clr
  assign controlled_buffer_1_out = ram_rd ? in_1 : 8'bz;  // Controlled_Buffer controlled_buffer_1
  assign controlled_inverter_1_out = imm2b ? ~rom_1_data : 8'bz;  // Controlled_Inverter controlled_inverter_1
  or or_1 (mem_rd, src_7, src_5, src_3);
  or or_2 (src_67, src_7, src_6);
  or or_3 (src_45, src_5, src_4);
  or or_4 (mem_wr, dst_7, dst_5, dst_3);
  or or_5 (mem, mem_wr, mem_rd);
  Decoder #(.select(3)) decoder_3 (
    .out0(decoder_3_out0), .out1(decoder_3_out1), .out2(decoder_3_out2), .out3(decoder_3_out3),
    .out4(decoder_3_out4), .out5(decoder_3_out5), .out6(decoder_3_out6), .out7(decoder_3_out7), .sel(src));  // open: en
  assign controlled_buffer_1_out = y_rd ? Y_q : 8'bz;  // Controlled_Buffer controlled_buffer_2
  Pull_Resistor pull_resistor_1 (.node(controlled_buffer_1_out));
  Pull_Resistor pull_resistor_2 (.node(controlled_inverter_1_out));
  Register register_1 (
    .D(pull_resistor_3_node), .en(not_2_out), .clk(clk), .Q({src, register_1_q[4], bit3, dst}));  // open: clr
  not not_1 (not_1_out, pc_wr);
  Pull_Resistor pull_resistor_3 (.node(pull_resistor_3_node));
  assign pull_resistor_3_node = not_1_out ? rom_1_data : 8'bz;  // Controlled_Buffer controlled_buffer_3
  not not_2 (not_2_out, imm2b);
  Register X (.D(alu_1_alu_out), .en(x_wr), .clk(clk), .Q(X_q));  // open: clr
  assign controlled_buffer_1_out = x_rd ? X_q : 8'bz;  // Controlled_Buffer controlled_buffer_4
  Register C (.D(alu_1_alu_out), .en(c_wr), .clk(clk), .Q(C_q));  // open: clr
  nor nor_1 (nor_1_out, src[0], src[1], src[2]);
  and and_1 (type1, bit3, ~register_1_q[4]);  // AND_Gate
  and and_2 (type0, ~bit3, ~register_1_q[4]);  // AND_Gate
  and and_3 (type2, ~bit3, register_1_q[4]);  // AND_Gate
  and and_4 (cmp, dst[0], ~dst[1], ~dst[2], ~register_1_q[4]);  // AND_Gate
  and and_5 (jump, ~dst[0], dst[1], dst[2], bit3, register_1_q[4]);  // AND_Gate
  and and_6 (branch, dst[0], dst[1], dst[2], bit3, register_1_q[4]);
  and and_7 (and_7_out, decoder_3_out5, flags[0]);
  and and_8 (and_8_out, decoder_3_out6, ~flags[0]);  // AND_Gate
  and and_9 (and_9_out, decoder_3_out0, flags[1]);
  and and_10 (and_10_out, decoder_3_out1, ~flags[1]);  // AND_Gate
  and and_11 (and_11_out, decoder_3_out2, flags[2]);
  and and_12 (and_12_out, decoder_3_out4, ~flags[2]);  // AND_Gate
  and and_13 (and_13_out, decoder_3_out7, flags[3]);
  and and_14 (and_14_out, decoder_3_out3, ~flags[3]);  // AND_Gate
  assign controlled_buffer_1_out = c_rd ? C_q : 8'bz;  // Controlled_Buffer controlled_buffer_5
  and and_15 (movi, ~addr, dst[1], ~dst[2], type1);  // AND_Gate
  and and_16 (and_16_out, jump, nor_1_out);
  and and_17 (nop, nor_1_out, type0);
  and and_18 (and_18_out, jump, blah, ~addr);  // AND_Gate
  or or_6 (or_6_out, and_7_out, and_8_out, and_9_out, and_10_out, and_11_out, and_12_out, and_13_out, and_14_out);
  Register u_B (.D(alu_1_alu_out), .en(b_wr), .clk(clk), .Q(B_q));  // open: clr
  assign not_3_out = ~controlled_buffer_1_out;  // NOT_Gate not_3, 8 bits wide
  nor nor_2 (nor_2_out, bit3, addr);
  Multiplexer #(.width(8)) multiplexer_1 (
    .in0(controlled_buffer_1_out), .in1(not_3_out), .out(multiplexer_1_out), .sel(invertB), .en(nor_2_out));
  or or_7 (or_7_out, movi, branch);
  or or_8 (imm, type1, branch, and_16_out);
  nor nor_3 (nor_3_out, addr, movi, type2);
  Pull_Resistor pull_resistor_4 (.node(opcode));
  assign opcode = nor_3_out ? {register_1_q[4], dst} : 4'bz;  // Controlled_Buffer controlled_buffer_6
  or or_9 (goto, jump, branch);
  and and_19 (and_19_out, branch, ~done, or_6_out);  // AND_Gate
  Register A (.D(alu_1_alu_out), .en(a_wr), .clk(clk), .Q(A_q));  // open: clr
  assign controlled_buffer_1_out = b_rd ? B_q : 8'bz;  // Controlled_Buffer controlled_buffer_7
  nor nor_4 (nor_4_out, nor_2_out, or_7_out);
  assign or_10_out = multiplexer_1_out | controlled_inverter_1_out;  // OR_Gate or_10, 8 bits wide
  or or_11 (pc_wr, and_18_out, and_19_out);
  assign controlled_buffer_8_out = a_rd ? A_q : 8'bz;  // Controlled_Buffer controlled_buffer_8
  Pull_Resistor pull_resistor_5 (.node(controlled_buffer_8_out));
  Pull_Resistor pull_resistor_6 (.node(pull_resistor_6_node));
  assign pull_resistor_6_node = nor_4_out ? controlled_buffer_1_out : 8'bz;  // Controlled_Buffer controlled_buffer_9
  assign or_12_out = pull_resistor_6_node | controlled_buffer_8_out;  // OR_Gate or_12, 8 bits wide
  assign b = or_10_out | or_12_out;  // OR_Gate or_13, 8 bits wide
  Register MAR (.D(alu_1_alu_out), .en(addr), .clk(clk), .Q(MAR_q));  // open: clr
  and and_20 (and_20_out, imm, ~done);  // AND_Gate
  or or_14 (or_14_out, and_20_out, addr);
  and and_21 (addr, ~done, mem);  // AND_Gate
  D_Flip_Flop d_ff_1 (.D(or_14_out), .clk(clk), .Q(d_ff_1_q));  // open: Qn, preset, reset
  assign controlled_buffer_10_out = bit3 ? {src_0, src_1, src_2, src_4, src_6, mem_rd} : 6'bz;  // Controlled_Buffer controlled_buffer_10
  Pull_Resistor pull_resistor_7 (.node(controlled_buffer_10_out));
  alu alu_1 (
    .carry_flag(flags[0]), .inputA(or_12_out), .inputB(or_10_out), .op(opcode), .alu_out(alu_1_alu_out),
    .flags(alu_1_flags), .invertB(invertB));
  D_Flip_Flop d_ff_2 (.D(and_22_out), .clk(clk), .Q(d_ff_2_q));  // open: Qn, preset, reset
  and and_22 (and_22_out, type1, d_ff_1_q, mem_rd);
  and and_23 (and_23_out, mem_rd, done);
  or or_15 (or_15_out, src_0, type0);
  or or_16 (or_16_out, controlled_buffer_10_out[0], mem_wr);
  or or_17 (or_17_out, controlled_buffer_10_out[1], dst_6);
  or or_18 (or_18_out, controlled_buffer_10_out[2], dst_4);
  or or_19 (or_19_out, controlled_buffer_10_out[3], dst_2);
  or or_20 (or_20_out, controlled_buffer_10_out[4], dst_1);
  or or_21 (or_21_out, controlled_buffer_10_out[5], type0, dst_0);
  or or_22 (done, d_ff_1_q, d_ff_2_q);
  or or_23 (imm2b, and_22_out, or_14_out);
  and and_24 (and_24_out, ~done, mem_wr);  // AND_Gate
  and and_25 (ram_rd, done, mem_rd);
  and and_26 (and_26_out, ~done, dst_7);  // AND_Gate
  and and_27 (and_27_out, ~and_24_out, ~and_23_out, src_67);  // AND_Gate
  and and_28 (and_28_out, ~done, dst_5);  // AND_Gate
  and and_29 (and_29_out, ~and_24_out, ~and_23_out, src_45);  // AND_Gate
  and and_30 (c_rd, ~and_24_out, src_2);  // AND_Gate
  and and_31 (b_rd, ~and_24_out, src_1);  // AND_Gate
  and and_32 (ram_wr, or_16_out, and_38_out);
  and and_33 (y_wr, or_17_out, and_38_out);
  and and_34 (x_wr, or_18_out, and_38_out);
  and and_35 (c_wr, or_19_out, and_38_out);
  and and_36 (b_wr, or_20_out, and_38_out);
  and and_37 (a_wr, or_21_out, and_38_out);
  and and_38 (and_38_out, ~cmp, wr_en);  // AND_Gate
  nor nor_5 (nor_5_out, type2, movi);
  assign controlled_buffer_11_out = wr_en ? alu_1_flags[0] : 1'bz;  // Controlled_Buffer controlled_buffer_11
  assign controlled_buffer_12_out = nor_5_out ? controlled_buffer_11_out : 1'bz;  // Controlled_Buffer controlled_buffer_12
  assign controlled_buffer_13_out = wr_en ? alu_1_flags[1] : 1'bz;  // Controlled_Buffer controlled_buffer_13
  assign controlled_buffer_14_out = wr_en ? alu_1_flags[2] : 1'bz;  // Controlled_Buffer controlled_buffer_14
  assign controlled_buffer_15_out = nor_5_out ? controlled_buffer_14_out : 1'bz;  // Controlled_Buffer controlled_buffer_15
  assign controlled_buffer_16_out = wr_en ? alu_1_flags[3] : 1'bz;  // Controlled_Buffer controlled_buffer_16
  and and_39 (and_39_out, imm, ~and_22_out, done);  // AND_Gate
  or or_24 (y_rd, and_26_out, and_27_out);
  or or_25 (x_rd, and_28_out, and_29_out);
  and and_40 (a_rd, or_15_out, ~addr, ~goto, ~movi);  // AND_Gate
  D_Flip_Flop d_ff_3 (.D(controlled_buffer_12_out), .clk(clk), .Q(flags[0]));  // open: Qn, preset, reset
  D_Flip_Flop d_ff_4 (.D(controlled_buffer_13_out), .clk(clk), .Q(flags[1]));  // open: Qn, preset, reset
  D_Flip_Flop d_ff_5 (.D(controlled_buffer_15_out), .clk(clk), .Q(flags[2]));  // open: Qn, preset, reset
  D_Flip_Flop d_ff_6 (.D(controlled_buffer_16_out), .clk(clk), .Q(flags[3]));  // open: Qn, preset, reset
  nor nor_6 (blah, and_39_out, addr, nop);
  and and_41 (wr_en, blah, ~goto);  // AND_Gate

  // Notes on the sheet:
  //   contents of rom_1 (hex, n*v repeats v):
  //   2a f5 f4 ff 90 80 22 42 7f ef 92 5c ca fd 1e eb 91 3d ca fe 30 42 1d 7f fd b0 ff
endmodule

module alu (
  input  carry_flag,
  input  [7:0] inputA,
  input  [7:0] inputB,
  input  [3:0] op,
  output [7:0] alu_out,
  output [3:0] flags,
  output invertB
);

  wire adder_1_cout, and_1_out, and_2_out, comparator_1_eq, comparator_1_gt, decoder_1_out0, decoder_1_out1,
       decoder_1_out2, decoder_1_out3, decoder_1_out4, decoder_1_out5, decoder_1_out6, decoder_1_out7,
       decoder_1_out8, decoder_1_out9, decoder_1_out10, decoder_1_out11, decoder_1_out12, decoder_1_out13,
       or_1_out, or_4_out, or_5_out, or_6_out, or_7_out, or_8_out, or_9_out, or_10_out, or_11_out,
       xnor_1_out, xor_1_out;
  wire [7:0] adder_1_out, and_3_out, multiplexer_1_out, or_3_out, shifter_1_out, shifter_2_out, xor_2_out;

  Pull_Resistor pull_resistor_1 (.node(inputA));
  Pull_Resistor pull_resistor_2 (.node(inputB));
  Multiplexer #(.enable("false"), .width(8)) multiplexer_1 (
    .in0(inputB), .in1({8{1'b1}}), .out(multiplexer_1_out), .sel(decoder_1_out13));
  and and_1 (and_1_out, carry_flag, or_4_out);
  or or_1 (or_1_out, and_1_out, or_5_out);
  Adder adder_1 (.a(inputA), .b(multiplexer_1_out), .out(adder_1_out), .cin(or_1_out), .cout(adder_1_cout));
  xor xor_1 (xor_1_out, adder_1_out[7], inputA[7]);
  xnor xnor_1 (xnor_1_out, inputA[7], multiplexer_1_out[7]);
  or or_2 (invertB, decoder_1_out13, decoder_1_out1, decoder_1_out3, decoder_1_out2);
  and and_2 (and_2_out, xor_1_out, xnor_1_out);
  assign and_3_out = inputA & multiplexer_1_out;  // AND_Gate and_3, 8 bits wide
  assign or_3_out = inputA | multiplexer_1_out;  // OR_Gate or_3, 8 bits wide
  assign xor_2_out = inputA ^ multiplexer_1_out;  // XOR_Gate xor_2, 8 bits wide
  Shifter shifter_1 (.in(inputA), .\dist (3'b001), .out(shifter_1_out));
  Shifter #(.shift("lr")) shifter_2 (.in(inputA), .\dist (3'b001), .out(shifter_2_out));
  Decoder #(.select(4)) decoder_1 (
    .out0(decoder_1_out0), .out1(decoder_1_out1), .out2(decoder_1_out2), .out3(decoder_1_out3),
    .out4(decoder_1_out4), .out5(decoder_1_out5), .out6(decoder_1_out6), .out7(decoder_1_out7),
    .out8(decoder_1_out8), .out9(decoder_1_out9), .out10(decoder_1_out10), .out11(decoder_1_out11),
    .out12(decoder_1_out12), .out13(decoder_1_out13), .sel(op));  // open: out14, out15, en
  or or_4 (or_4_out, decoder_1_out4, decoder_1_out3);
  or or_5 (or_5_out, decoder_1_out2, decoder_1_out1, decoder_1_out12);
  or or_6 (or_6_out, decoder_1_out12, decoder_1_out13, or_7_out);
  or or_7 (or_7_out, decoder_1_out0, decoder_1_out4, decoder_1_out2, decoder_1_out3, decoder_1_out1);
  assign alu_out = or_6_out ? adder_1_out : 8'bz;  // Controlled_Buffer controlled_buffer_1
  assign flags[0] = or_7_out ? adder_1_cout : 1'bz;  // Controlled_Buffer controlled_buffer_2
  assign flags[2] = or_7_out ? and_2_out : 1'bz;  // Controlled_Buffer controlled_buffer_3
  assign alu_out = decoder_1_out5 ? and_3_out : 8'bz;  // Controlled_Buffer controlled_buffer_4
  assign alu_out = decoder_1_out6 ? or_3_out : 8'bz;  // Controlled_Buffer controlled_buffer_5
  assign alu_out = decoder_1_out7 ? xor_2_out : 8'bz;  // Controlled_Buffer controlled_buffer_6
  assign alu_out = or_8_out ? shifter_1_out : 8'bz;  // Controlled_Buffer controlled_buffer_7
  or or_8 (or_8_out, decoder_1_out8, decoder_1_out10);
  assign flags[0] = or_8_out ? inputA[7] : 1'bz;  // Controlled_Buffer controlled_buffer_8
  assign alu_out = or_9_out ? shifter_2_out : 8'bz;  // Controlled_Buffer controlled_buffer_9
  or or_9 (or_9_out, decoder_1_out9, decoder_1_out11);
  assign flags[0] = or_9_out ? inputA[0] : 1'bz;  // Controlled_Buffer controlled_buffer_10
  or or_10 (or_10_out, decoder_1_out5, decoder_1_out6, decoder_1_out7, decoder_1_out12, decoder_1_out13);
  Comparator comparator_1 (.a({8{1'b0}}), .b(alu_out), .gt(comparator_1_gt), .eq(comparator_1_eq));  // open: lt
  assign flags[3] = or_11_out ? comparator_1_gt : 1'bz;  // Controlled_Buffer controlled_buffer_11
  assign flags[1] = or_11_out ? comparator_1_eq : 1'bz;  // Controlled_Buffer controlled_buffer_12
  or or_11 (or_11_out, or_6_out, or_8_out, or_9_out, or_10_out);
endmodule
