// Logisim project cpu.circ as structural Verilog: 3 circuits, main circuit main
module main (
  input  [7:0] in_1,
  input  [7:0] a,
  input  [7:0] b,
  input  fwd_b,
  input  fwd_a,
  input  [2:0] ra,
  input  [2:0] rb,
  input  useimm5,
  input  useimm8,
  input  invb,
  input  [7:0] imm,
  output [7:0] out_12
);

  wire button_1_out, not_1_out, not_3_out;
  wire [7:0] bit_extender_1_out, multiplexer_1_out, multiplexer_2_out, multiplexer_3_out, not_2_out, undriven;

  Button button_1 (.out(button_1_out));
  regs regs_1 (.data(undriven), .wr_sel(ra), .a_rd(ra), .b_rd(rb), .reset(button_1_out));  // open: a, b
  Multiplexer #(.disabled("Z"), .enable("true"), .width(8)) multiplexer_1 (
    .in0(a), .in1(in_1), .out(multiplexer_1_out), .sel(fwd_a), .en(not_1_out));
  not not_1 (not_1_out, useimm5);
  Multiplexer #(.width(8)) multiplexer_2 (.in0(b), .in1(in_1), .out(multiplexer_2_out), .sel(fwd_b));
  Multiplexer #(.enable("true"), .width(8)) multiplexer_3 (
    .in0(multiplexer_2_out), .in1(not_2_out), .out(multiplexer_3_out), .sel(invb), .en(not_3_out));
  assign not_2_out = ~multiplexer_2_out;  // NOT_Gate not_2, 8 bits wide
  not not_3 (not_3_out, useimm8);
  assign multiplexer_3_out = useimm8 ? imm : 8'bz;  // Controlled_Buffer controlled_buffer_1
  assign multiplexer_1_out = useimm5 ? bit_extender_1_out : 8'bz;  // Controlled_Buffer controlled_buffer_2
  assign bit_extender_1_out = {{3{imm[4]}}, imm[4:0]};  // Bit_Extender bit_extender_1
  Adder adder_1 (.a(multiplexer_1_out), .b(multiplexer_3_out), .out(out_12));  // open: cin, cout
endmodule

module regs (
  input  [7:0] data,
  input  [2:0] wr_sel,
  input  [2:0] a_rd,
  input  [2:0] b_rd,
  input  reset,
  output [7:0] a,
  output [7:0] b
);

  wire clock_1_out, decoder_1_out0, decoder_1_out1, decoder_1_out2, decoder_1_out3, decoder_1_out4,
       decoder_1_out5, decoder_1_out6, decoder_1_out7;
  wire [7:0] register_1_q, register_2_q, register_3_q, register_4_q, register_5_q, register_6_q,
       register_7_q, register_8_q;

  Decoder #(.enable("false"), .select(3)) decoder_1 (
    .out0(decoder_1_out0), .out1(decoder_1_out1), .out2(decoder_1_out2), .out3(decoder_1_out3),
    .out4(decoder_1_out4), .out5(decoder_1_out5), .out6(decoder_1_out6), .out7(decoder_1_out7), .sel(wr_sel));
  Clock clock_1 (.out(clock_1_out));
  Register #(.trigger("falling")) register_1 (
    .D(data), .en(decoder_1_out0), .clk(clock_1_out), .Q(register_1_q), .clr(reset));
  Register #(.trigger("falling")) register_2 (
    .D(data), .en(decoder_1_out1), .clk(clock_1_out), .Q(register_2_q), .clr(reset));
  Register #(.trigger("falling")) register_3 (
    .D(data), .en(decoder_1_out2), .clk(clock_1_out), .Q(register_3_q), .clr(reset));
  Register #(.trigger("falling")) register_4 (
    .D(data), .en(decoder_1_out3), .clk(clock_1_out), .Q(register_4_q), .clr(reset));
  Register #(.trigger("falling")) register_5 (
    .D(data), .en(decoder_1_out4), .clk(clock_1_out), .Q(register_5_q), .clr(reset));
  Register #(.trigger("falling")) register_6 (
    .D(data), .en(decoder_1_out5), .clk(clock_1_out), .Q(register_6_q), .clr(reset));
  Register #(.trigger("falling")) register_7 (
    .D(data), .en(decoder_1_out6), .clk(clock_1_out), .Q(register_7_q), .clr(reset));
  Register #(.trigger("falling")) register_8 (
    .D(data), .en(decoder_1_out7), .clk(clock_1_out), .Q(register_8_q), .clr(reset));
  Multiplexer #(.select(3), .width(8)) multiplexer_1 (
    .in0(register_1_q), .in1(register_2_q), .in2(register_3_q), .in3(register_4_q), .in4(register_5_q),
    .in5(register_6_q), .in6(register_7_q), .in7(register_8_q), .out(a), .sel(b_rd));
  Multiplexer #(.select(3), .width(8)) multiplexer_2 (
    .in0(register_1_q), .in1(register_2_q), .in2(register_3_q), .in3(register_4_q), .in4(register_5_q),
    .in5(register_6_q), .in6(register_7_q), .in7(register_8_q), .out(b), .sel(a_rd));
endmodule

module dataloop (
  input  [7:0] writeback,
  input  [7:0] a,
  input  [7:0] b,
  input  fwd_b,
  input  fwd_a,
  input  disable_a,
  input  useimm5,
  input  useimm8,
  input  invb,
  input  [7:0] imm,
  output [7:0] out_11
);

  wire nor_1_out, not_2_out;
  wire [7:0] bit_extender_1_out, multiplexer_1_out, multiplexer_2_out, multiplexer_3_out, not_1_out;

  Multiplexer #(.disabled("Z"), .enable("true"), .width(8)) multiplexer_1 (
    .in0(a), .in1(writeback), .out(multiplexer_1_out), .sel(fwd_a), .en(nor_1_out));
  Multiplexer #(.width(8)) multiplexer_2 (.in0(b), .in1(writeback), .out(multiplexer_2_out), .sel(fwd_b));
  nor nor_1 (nor_1_out, disable_a, useimm5);
  Multiplexer #(.enable("true"), .width(8)) multiplexer_3 (
    .in0(multiplexer_2_out), .in1(not_1_out), .out(multiplexer_3_out), .sel(invb), .en(not_2_out));
  assign not_1_out = ~multiplexer_2_out;  // NOT_Gate not_1, 8 bits wide
  not not_2 (not_2_out, useimm8);
  assign multiplexer_3_out = useimm8 ? imm : 8'bz;  // Controlled_Buffer controlled_buffer_1
  assign multiplexer_1_out = useimm5 ? bit_extender_1_out : 8'bz;  // Controlled_Buffer controlled_buffer_2
  assign bit_extender_1_out = {{3{imm[4]}}, imm[4:0]};  // Bit_Extender bit_extender_1
  Adder adder_1 (.a(multiplexer_1_out), .b(multiplexer_3_out), .out(out_11));  // open: cin, cout
endmodule
